// Logisim project Guoyanduo.circ as structural Verilog: 4 circuits, main circuit main
module main (
  output [15:0] out_1
);

  wire and_1_out, and_2_out, and_3_out, and_4_out, and_5_out, and_6_out, and_7_out, and_8_out, and_9_out,
       and_10_out, and_11_out, and_12_out, clk, not_1_out, not_2_out, not_3_out, not_4_out, not_5_out,
       not_6_out, not_7_out, not_8_out, not_9_out, not_10_out, not_11_out, not_12_out, not_13_out,
       not_14_out, not_15_out, not_16_out, R0, R1, R2, R3;
  wire [15:0] alu_add_1_out_3, alu_add_2_out_3, alu_sub_1_out_3, and_13_out, and_14_out, and_15_out,
       and_16_out, and_17_out, and_18_out, and_19_out, and_20_out, and_21_out, and_22_out, and_23_out,
       and_24_out, and_25_out, bit_extender_1_out, bit_extender_2_out, bit_extender_3_out,
       bit_extender_4_out, bit_extender_5_out, bit_extender_6_out, bit_extender_7_out, bit_extender_8_out,
       bit_extender_9_out, bit_extender_10_out, bit_extender_11_out, bit_extender_12_out, or_1_out, PC_q,
       R0out, R1out, R2out, R3out, RegIn, rsOUT, rtOUT;

  Clock clock_1 (.out(clk));
  Register #(.width(16)) PC (.D(alu_add_1_out_3), .clk(clk), .Q(PC_q));  // open: en, clr
  ROM #(.addrWidth(16), .dataWidth(16)) mem (.addr(PC_q), .data(out_1));
  Register #(.width(16)) u_R0 (.D(RegIn), .en(R0), .clk(clk), .Q(R0out));  // open: clr
  Register #(.width(16)) u_R1 (.D(RegIn), .en(R1), .clk(clk), .Q(R1out));  // open: clr
  Register #(.width(16)) u_R2 (.D(RegIn), .en(R2), .clk(clk), .Q(R2out));  // open: clr
  Register #(.width(16)) u_R3 (.D(RegIn), .en(R3), .clk(clk), .Q(R3out));  // open: clr
  ALU_ADD alu_add_1 (.A(16'h1), .B(PC_q), .out_3(alu_add_1_out_3));
  not not_1 (not_1_out, out_1[11]);
  not not_2 (not_2_out, out_1[10]);
  not not_3 (not_3_out, out_1[11]);
  not not_4 (not_4_out, out_1[10]);
  not not_5 (not_5_out, out_1[9]);
  not not_6 (not_6_out, out_1[8]);
  not not_7 (not_7_out, out_1[9]);
  not not_8 (not_8_out, out_1[8]);
  and and_1 (and_1_out, not_1_out, not_2_out);
  and and_2 (and_2_out, not_3_out, out_1[10]);
  and and_3 (and_3_out, out_1[11], not_4_out);
  and and_4 (and_4_out, out_1[11], out_1[10]);
  and and_5 (and_5_out, not_5_out, not_6_out);
  and and_6 (and_6_out, not_7_out, out_1[8]);
  and and_7 (and_7_out, out_1[9], not_8_out);
  and and_8 (and_8_out, out_1[9], out_1[8]);
  not not_9 (not_9_out, out_1[1]);
  not not_10 (not_10_out, out_1[0]);
  not not_11 (not_11_out, out_1[1]);
  not not_12 (not_12_out, out_1[0]);
  assign bit_extender_1_out = {{15{and_1_out}}, and_1_out};  // Bit_Extender bit_extender_1
  assign bit_extender_2_out = {{15{and_2_out}}, and_2_out};  // Bit_Extender bit_extender_2
  assign bit_extender_3_out = {{15{and_3_out}}, and_3_out};  // Bit_Extender bit_extender_3
  assign bit_extender_4_out = {{15{and_4_out}}, and_4_out};  // Bit_Extender bit_extender_4
  assign bit_extender_5_out = {{15{and_5_out}}, and_5_out};  // Bit_Extender bit_extender_5
  assign bit_extender_6_out = {{15{and_6_out}}, and_6_out};  // Bit_Extender bit_extender_6
  assign bit_extender_7_out = {{15{and_7_out}}, and_7_out};  // Bit_Extender bit_extender_7
  assign bit_extender_8_out = {{15{and_8_out}}, and_8_out};  // Bit_Extender bit_extender_8
  and and_9 (and_9_out, not_9_out, not_10_out);
  and and_10 (and_10_out, not_11_out, out_1[0]);
  and and_11 (and_11_out, out_1[1], not_12_out);
  and and_12 (and_12_out, out_1[1], out_1[0]);
  assign and_13_out = R0out & bit_extender_1_out;  // AND_Gate and_13, 16 bits wide
  assign and_14_out = R1out & bit_extender_2_out;  // AND_Gate and_14, 16 bits wide
  assign and_15_out = R2out & bit_extender_3_out;  // AND_Gate and_15, 16 bits wide
  assign and_16_out = R3out & bit_extender_4_out;  // AND_Gate and_16, 16 bits wide
  assign and_17_out = R0out & bit_extender_5_out;  // AND_Gate and_17, 16 bits wide
  assign and_18_out = R1out & bit_extender_6_out;  // AND_Gate and_18, 16 bits wide
  assign and_19_out = R2out & bit_extender_7_out;  // AND_Gate and_19, 16 bits wide
  assign and_20_out = R3out & bit_extender_8_out;  // AND_Gate and_20, 16 bits wide
  assign or_1_out = rsOUT | rtOUT;  // OR_Gate or_1, 16 bits wide
  assign bit_extender_9_out = {{15{and_9_out}}, and_9_out};  // Bit_Extender bit_extender_9
  assign and_21_out = rsOUT & rtOUT;  // AND_Gate and_21, 16 bits wide
  assign bit_extender_10_out = {{15{and_10_out}}, and_10_out};  // Bit_Extender bit_extender_10
  ALU_ADD alu_add_2 (.A(rsOUT), .B(rtOUT), .out_3(alu_add_2_out_3));
  assign bit_extender_11_out = {{15{and_11_out}}, and_11_out};  // Bit_Extender bit_extender_11
  assign bit_extender_12_out = {{15{and_12_out}}, and_12_out};  // Bit_Extender bit_extender_12
  assign and_22_out = or_1_out & bit_extender_9_out;  // AND_Gate and_22, 16 bits wide
  ALU_SUB alu_sub_1 (.in_1(rsOUT), .in_2(rtOUT), .out_3(alu_sub_1_out_3));
  assign rsOUT = and_13_out | and_14_out | and_15_out | and_16_out;  // OR_Gate or_2, 16 bits wide
  assign rtOUT = and_17_out | and_18_out | and_19_out | and_20_out;  // OR_Gate or_3, 16 bits wide
  assign and_23_out = and_21_out & bit_extender_10_out;  // AND_Gate and_23, 16 bits wide
  assign and_24_out = alu_add_2_out_3 & bit_extender_11_out;  // AND_Gate and_24, 16 bits wide
  assign and_25_out = alu_sub_1_out_3 & bit_extender_12_out;  // AND_Gate and_25, 16 bits wide
  assign RegIn = and_22_out | and_23_out | and_24_out | and_25_out;  // OR_Gate or_4, 16 bits wide
  not not_13 (not_13_out, out_1[7]);
  not not_14 (not_14_out, out_1[6]);
  not not_15 (not_15_out, out_1[7]);
  not not_16 (not_16_out, out_1[6]);
  and and_26 (R0, not_13_out, not_14_out);
  and and_27 (R1, not_15_out, out_1[6]);
  and and_28 (R2, out_1[7], not_16_out);
  and and_29 (R3, out_1[7], out_1[6]);

  // Other names for the same wires on the sheet: funct[2:0] = {out_1[0], out_1[1], out_1[2]};
  //   imm[7:0] = {{3{out_1[2]}}, out_1[3], out_1[4], out_1[5], out_1[6], out_1[7]}; rd[1:0] = {out_1[6], out_1[7]};
  //   opcode[3:0] = {out_1[12], out_1[13], out_1[14], out_1[15]}; rs[1:0] = {out_1[10], out_1[11]};
  //   rt[1:0] = {out_1[8], out_1[9]}

  // Notes on the sheet:
  //   contents of mem (hex, n*v repeats v):
  //   d00 592*0 111 0 0 0 101
endmodule

module ALU_ADD (
  input  [15:0] A,
  input  [15:0] B,
  output [15:0] out_3
);

  wire onebitadder_1_up, onebitadder_2_up, onebitadder_3_up, onebitadder_4_up, onebitadder_5_up,
       onebitadder_6_up, onebitadder_7_up, onebitadder_8_up, onebitadder_9_up, onebitadder_10_up,
       onebitadder_11_up, onebitadder_12_up, onebitadder_13_up, onebitadder_14_up, onebitadder_15_up;

  oneBitAdder onebitadder_1 (.a(A[0]), .b(B[0]), .isup(1'b0), .RES(out_3[0]), .UP(onebitadder_1_up));
  oneBitAdder onebitadder_2 (.a(A[1]), .b(B[1]), .isup(onebitadder_1_up), .RES(out_3[1]), .UP(onebitadder_2_up));
  oneBitAdder onebitadder_3 (.a(A[2]), .b(B[2]), .isup(onebitadder_2_up), .RES(out_3[2]), .UP(onebitadder_3_up));
  oneBitAdder onebitadder_4 (.a(A[3]), .b(B[3]), .isup(onebitadder_3_up), .RES(out_3[3]), .UP(onebitadder_4_up));
  oneBitAdder onebitadder_5 (.a(A[4]), .b(B[4]), .isup(onebitadder_4_up), .RES(out_3[4]), .UP(onebitadder_5_up));
  oneBitAdder onebitadder_6 (.a(A[5]), .b(B[5]), .isup(onebitadder_5_up), .RES(out_3[5]), .UP(onebitadder_6_up));
  oneBitAdder onebitadder_7 (.a(A[6]), .b(B[6]), .isup(onebitadder_6_up), .RES(out_3[6]), .UP(onebitadder_7_up));
  oneBitAdder onebitadder_8 (.a(A[7]), .b(B[7]), .isup(onebitadder_7_up), .RES(out_3[7]), .UP(onebitadder_8_up));
  oneBitAdder onebitadder_9 (.a(A[8]), .b(B[8]), .isup(onebitadder_8_up), .RES(out_3[8]), .UP(onebitadder_9_up));
  oneBitAdder onebitadder_10 (.a(A[9]), .b(B[9]), .isup(onebitadder_9_up), .RES(out_3[9]), .UP(onebitadder_10_up));
  oneBitAdder onebitadder_11 (.a(A[10]), .b(B[10]), .isup(onebitadder_10_up), .RES(out_3[10]), .UP(onebitadder_11_up));
  oneBitAdder onebitadder_12 (.a(A[11]), .b(B[11]), .isup(onebitadder_11_up), .RES(out_3[11]), .UP(onebitadder_12_up));
  oneBitAdder onebitadder_13 (.a(A[12]), .b(B[12]), .isup(onebitadder_12_up), .RES(out_3[12]), .UP(onebitadder_13_up));
  oneBitAdder onebitadder_14 (.a(A[13]), .b(B[13]), .isup(onebitadder_13_up), .RES(out_3[13]), .UP(onebitadder_14_up));
  oneBitAdder onebitadder_15 (.a(A[14]), .b(B[14]), .isup(onebitadder_14_up), .RES(out_3[14]), .UP(onebitadder_15_up));
  oneBitAdder onebitadder_16 (.a(A[15]), .b(B[15]), .isup(onebitadder_15_up), .RES(out_3[15]));  // open: UP
endmodule

module oneBitAdder (
  input  a,
  input  b,
  input  isup,
  output RES,
  output UP
);

  wire and_1_out, and_2_out, and_3_out, or_1_out, xor_1_out;

  and and_1 (and_1_out, a, isup);
  and and_2 (and_2_out, b, isup);
  and and_3 (and_3_out, a, b);
  or or_1 (or_1_out, and_2_out, and_1_out);
  xor xor_1 (xor_1_out, a, b);
  or or_2 (UP, and_3_out, or_1_out);
  xor xor_2 (RES, xor_1_out, isup);
endmodule

module ALU_SUB (
  input  [15:0] in_1,
  input  [15:0] in_2,
  output [15:0] out_3
);

  wire [15:0] alu_add_1_out_3, xor_1_out;

  assign xor_1_out = in_2 ^ {16{1'b1}};  // XOR_Gate xor_1, 16 bits wide
  ALU_ADD alu_add_1 (.A(xor_1_out), .B(16'h1), .out_3(alu_add_1_out_3));
  ALU_ADD alu_add_2 (.A(in_1), .B(alu_add_1_out_3), .out_3(out_3));
endmodule
